# Fritzing sketch fritzing-sketch (saved by Fritzing 0.9.3b)
breadboards: 1

parts:
  U1 = NodeMCU V3.0
  S1 = Momentary Switch [package=ksa_sealed_tac_switch]
  R1 = Resistor [tolerance=±5% resistance=1k package=THT]

nets:
  N1: U1.D1, S1.2, R1.Pin_1
  N2: U1.3V3, S1.3
  N3: U1.GND#6, U1.GND#13, U1.GND#16, U1.GND#33, R1.Pin_0

custom parts:
  NodeMCU V3.0: ESP8266 based NodeMCU
